# Fritzing sketch Full Stripboard Layout (saved by Fritzing 0.8.7b)
stripboards: 1

parts:
  Q1 = Basic FET N-Channel [package="TO220 [THT]"]
  Q2 = Basic FET N-Channel [package="TO220 [THT]"]
  Q3 = Basic FET N-Channel [package="TO220 [THT]"]
  R1 = Resistor [tolerance=±5% resistance=220 package=THT]
  R2 = Resistor [tolerance=±5% resistance=220 package=THT]
  R3 = Resistor [tolerance=±5% resistance=220 package=THT]
  R4 = Resistor [tolerance=±5% resistance=1k package=THT]
  R5 = Resistor [tolerance=±5% resistance=1k package=THT]
  R6 = Vertical Resistor [tolerance=±5% resistance=220 package=THT]
  DPDT_Relay1 = IC, DIP package, 16 pins [chip_label=GS-SH-212D]
  DPDT_Relay2 = IC, DIP package, 16 pins [chip_label=GS-SH-212D]
  Q4 = Basic FET N-Channel [package="TO220 [THT]"]
  Q5 = Basic FET N-Channel [package="TO220 [THT]"]
  R7 = Vertical Resistor [tolerance=±5% resistance=220 package=THT]
  R8 = Vertical Resistor [tolerance=±5% resistance=220 package=THT]  # not connected
  R9 = Vertical Resistor [tolerance=±5% resistance=220 package=THT]  # not connected
  R10 = Vertical Resistor [tolerance=±5% resistance=220 package=THT]
  R11 = Vertical Resistor [tolerance=±5% resistance=220 package=THT]  # not connected
  R12 = Vertical Resistor [tolerance=±5% resistance=220 package=THT]
  R13 = Vertical Resistor [tolerance=±5% resistance=220 package=THT]  # not connected
  R14 = Vertical Resistor [tolerance=±5% resistance=220 package=THT]
  R15 = Resistor [tolerance=±5% resistance=6.8k package=THT]

nets:
  N1: Q1.gate, R1.Pin_0
  N2: Q1.source, Q2.source, Q3.source, R4.Pin_1, R5.Pin_1, R6.Pin_1, DPDT_Relay1.pin2, DPDT_Relay1.pin15, DPDT_Relay2.pin2, DPDT_Relay2.pin15, Q4.source, Q5.source, R10.Pin_0, R12.Pin_0, R14.Pin_0, R14.Pin_1
  N3: Q2.gate, R2.Pin_0
  N4: Q3.gate, R3.Pin_0
  N5: R1.Pin_1, R4.Pin_0
  N6: R2.Pin_1, R5.Pin_0
  N7: R3.Pin_1, R6.Pin_0
  N8: DPDT_Relay1.pin1, DPDT_Relay1.pin16, DPDT_Relay2.pin1, DPDT_Relay2.pin16, Q4.drain, Q5.drain
  N9: DPDT_Relay1.pin3, DPDT_Relay1.pin14
  N10: DPDT_Relay1.pin4, DPDT_Relay1.pin13
  N11: DPDT_Relay1.pin5, DPDT_Relay1.pin12
  N12: DPDT_Relay1.pin6, DPDT_Relay1.pin11
  N13: DPDT_Relay1.pin7, DPDT_Relay1.pin10
  N14: DPDT_Relay1.pin8, DPDT_Relay1.pin9
  N15: DPDT_Relay2.pin3, DPDT_Relay2.pin14
  N16: DPDT_Relay2.pin4, DPDT_Relay2.pin13
  N17: DPDT_Relay2.pin5, DPDT_Relay2.pin12
  N18: DPDT_Relay2.pin6, DPDT_Relay2.pin11
  N19: DPDT_Relay2.pin7, DPDT_Relay2.pin10
  N20: DPDT_Relay2.pin8, DPDT_Relay2.pin9, R15.Pin_0, R15.Pin_1
  N21: Q4.gate, R7.Pin_1
  N22: Q5.gate, R12.Pin_1
  N23: R7.Pin_0, R10.Pin_1

custom parts:
  Vertical Resistor: A generic resistor (0.25W)
