# Fritzing sketch LED Driving (saved by Fritzing 0.8.7b)
breadboards: 1

parts:
  Q1 = Basic FET N-Channel [package="TO220 [THT]"]
  Q2 = Basic FET N-Channel [package="TO220 [THT]"]
  Q3 = Basic FET N-Channel [package="TO220 [THT]"]
  R1 = Resistor [tolerance=±5% resistance=220 package=THT]
  R2 = Resistor [tolerance=±5% resistance=220 package=THT]
  R3 = Resistor [tolerance=±5% resistance=220 package=THT]
  RGB_Strip_LED1 = RGB Strip LED
  Part1 = Arduino Uno (Rev3)

nets:
  N1: Q1.gate, RGB_Strip_LED1.Blue_Connect#5
  N2: Q1.drain, R1.Pin_0
  N3: Q1.source, Q2.source, Q3.source
  N4: Q2.gate, RGB_Strip_LED1.Green_Connect#7
  N5: Q2.drain, R2.Pin_0
  N6: Q3.gate, RGB_Strip_LED1.Red_Connect#6
  N7: Q3.drain, R3.Pin_0
  N8: R1.Pin_1, Part1.D11_PWM/MOSI
  N9: R2.Pin_1, Part1.D10_PWM/SS
  N10: R3.Pin_1, Part1.D9_PWM

custom parts:
  RGB Strip LED: A tri-color Strip LED with red, green and blue. Pin order: red - common cathode - blue - green
