# Fritzing sketch TestSetUpFritzing (saved by Fritzing 0.8.7b)
breadboards: 1

parts:
  Part1 = Arduino Motor Shield (Rev3)
  Part2 = Arduino Uno (Rev3)  # not connected
  LED6 = LED - 5mm [color="Red (633nm)" package="5 mm [THT]"]
  LED5 = LED - 5mm [color="Red (633nm)" package="5 mm [THT]"]
  LED4 = LED - 5mm [color="Red (633nm)" package="5 mm [THT]"]
  LED3 = LED - 5mm [color="Red (633nm)" package="5 mm [THT]"]
  LED1 = LED - 5mm [color="Red (633nm)" package="5 mm [THT]"]
  LED2 = LED - 5mm [color="Red (633nm)" package="5 mm [THT]"]
  R1 = Resistor [tolerance=±5% resistance=220 package=THT]
  R2 = Resistor [tolerance=±5% resistance=220 package=THT]
  R3 = Resistor [tolerance=±5% resistance=220 package=THT]  # not connected
  R4 = Resistor [tolerance=±5% resistance=220 package=THT]
  R5 = Resistor [tolerance=±5% resistance=220 package=THT]
  R6 = Resistor [tolerance=±5% resistance=220 package=THT]
  LED7 = RGB LED (com. anode, rbg) [package="5 mm [THT]"]
  R7 = Resistor [tolerance=±5% resistance=220 package=THT]
  R8 = Resistor [tolerance=±5% resistance=220 package=THT]
  R9 = Resistor [tolerance=±5% resistance=220 package=THT]
  M1 = Stepper Motor - Bipolar

nets:
  N1: Part1.GND, LED2.cathode, LED7.common_anode
  N2: Part1.B-, M1.D
  N3: Part1.B+, M1.B
  N4: Part1.A-, M1.C
  N5: Part1.A+, M1.A
  N6: Part1.5V, LED6.cathode, LED5.anode, LED4.cathode, LED1.cathode, R2.Pin_0, R5.Pin_0
  N7: LED6.anode, R6.Pin_0
  N8: LED5.cathode, LED4.anode, R4.Pin_0
  N9: LED3.cathode, LED1.anode
  N10: R1.Pin_0, R6.Pin_1
  N11: R1.Pin_1, R5.Pin_1
  N12: LED7.red_cathode, R7.Pin_0
  N13: LED7.blue_cathode, R8.Pin_0, R9.Pin_0
  N14: R8.Pin_1, R9.Pin_1
