# Fritzing sketch StepTestingFritzing (saved by Fritzing 0.8.7b)

parts:
  Part1 = Arduino Motor Shield (Rev3)
  J1 = Power Jack [package=power_jack_slot]
  M1 = Stepper Motor - Bipolar

nets:
  GND: Part1.GND, Part1.D3_PWM/A, J1.GND
  N1: Part1.B-, M1.D
  N2: Part1.B+, M1.B
  N3: Part1.A-, M1.C
  N4: Part1.A+, M1.A
  N5: Part1.VMOT, Part1.VIN, J1.PWR
